// Logisim project MIPS.circ as structural Verilog: 1 circuit, main circuit main
module main (
  input  Branch,
  input  RegDst,
  input  ALUSrc,
  input  RegWrite,
  input  MemWrite,
  input  MemtoReg,
  input  [2:0] ALUControl
);

  wire alu_1_zero, and_1_out, button_1_out, CLK;
  wire [4:0] multiplexer_2_out, rom_1_data_2;
  wire [7:0] adder_1_out, multiplexer_1_out, PC_q;
  wire [31:0] adder_2_out, alu_1_alu_result, bit_extender_1_out, bit_extender_2_out, data_mem_1_rd,
       multiplexer_3_out, multiplexer_4_out, regfile32_1_rd1, regfile32_1_rd2, rom_1_data, shifter_1_out;

  Clock clock_1 (.out(CLK));
  // Probe on adder_1_out
  Multiplexer #(.width(8)) multiplexer_1 (
    .in0(adder_1_out), .in1(adder_2_out[7:0]), .out(multiplexer_1_out), .sel(and_1_out));  // open: en
  Button button_1 (.out(button_1_out));
  // Probe on adder_2_out[7:0]
  Register PC (.D(multiplexer_1_out), .Q(PC_q), .clk(CLK), .clr(button_1_out));  // open: en
  Adder adder_1 (.a(PC_q), .b(8'h4), .out(adder_1_out));  // open: cin, cout
  // Probe on rom_1_data_2
  ROM #(.addrWidth(6), .dataWidth(32)) rom_1 (
    .addr(PC_q[7:2]), .data({rom_1_data[31:26], rom_1_data_2, rom_1_data[20:0]}));  // open: sel
  assign bit_extender_1_out = {{24{1'b0}}, adder_1_out};  // Bit_Extender bit_extender_1
  assign bit_extender_2_out = {{16{rom_1_data[15]}}, rom_1_data[15:0]};  // Bit_Extender bit_extender_2
  RegFile32 regfile32_1 (
    .AD1(rom_1_data_2), .AD2(rom_1_data[20:16]), .CLK(CLK), .WE(RegWrite), .AD3(multiplexer_2_out),
    .WD3(multiplexer_4_out), .RD1(regfile32_1_rd1), .RD2(regfile32_1_rd2));
  Multiplexer #(.width(5)) multiplexer_2 (
    .in0(rom_1_data[20:16]), .in1(rom_1_data[15:11]), .out(multiplexer_2_out), .sel(RegDst));  // open: en
  Multiplexer #(.width(32)) multiplexer_3 (
    .in0(regfile32_1_rd2), .in1(bit_extender_2_out), .out(multiplexer_3_out), .sel(ALUSrc));  // open: en
  // Probe on bit_extender_2_out
  ALU alu_1 (
    .SrcA(regfile32_1_rd1), .SrcB(multiplexer_3_out), .ALU_Control(ALUControl), .Zero(alu_1_zero),
    .ALU_Result(alu_1_alu_result));
  // Probe on shifter_1_out
  // Probe on bit_extender_1_out
  Shifter #(.width(32)) shifter_1 (.in(bit_extender_2_out), .\dist (5'b00010), .out(shifter_1_out));
  and and_1 (and_1_out, Branch, alu_1_zero);
  Adder #(.width(32)) adder_2 (.a(shifter_1_out), .b(bit_extender_1_out), .out(adder_2_out));  // open: cin, cout
  Data_Mem data_mem_1 (.A(alu_1_alu_result), .CLK(CLK), .WE(MemWrite), .WD(regfile32_1_rd2), .RD(data_mem_1_rd));
  Multiplexer #(.width(32)) multiplexer_4 (
    .in0(alu_1_alu_result), .in1(data_mem_1_rd), .out(multiplexer_4_out), .sel(MemtoReg));  // open: en

  // Notes on the sheet:
  //   A AND NOT B : 100
  //   A OR NOT B : 101
  //   AND : 000
  //   OR : 001
  //   + : 010
  //   A - B : 110
  //   SLT : 111
  //   lw t0 0x00(zero)
  //   lw t1 0x00(zero)
  //   beq t0 t1 0xffffffff 
  //   contents of rom_1 (hex, n*v repeats v):
  //   8c080000 8c090000 1109ffff
endmodule
